// Logisim project cpu.circ as structural Verilog: 9 circuits, main circuit CPU
module CPU (
  output halt,
  output [47:0] cpu_out
);

  wire alu_1_negative, alu_1_overflow, alu_1_zero, and_1_out, and_2_out, and_3_out, clk_out, comparator_1_eq,
       conditionencoding_1_c, decoder_1_out0, decoder_1_out1, decoder_1_out2, decoder_1_out3, decoder_1_out4,
       decoder_2_out0, decoder_2_out1, decoder_2_out2, decoder_2_out3, or_1_out, or_2_out, or_3_out,
       reset_out;
  wire [2:0] adder_1_out, Counter_q, multiplexer_1_out, multiplexer_3_out, multiplexer_4_out;
  wire [15:0] adder_2_out, alu_1_c, bit_extender_1_out, bit_extender_2_out, InsMem_data, multiplexer_2_out,
       multiplexer_5_out, multiplexer_6_out, RA_q, ram_1_dout, RB_q, RD_q, registerfile_1_a,
       registerfile_1_b, RW_q;

  Clock clk (.out(clk_out));
  Button reset (.out(reset_out));
  Multiplexer #(.width(3)) multiplexer_1 (.in0(adder_1_out), .in1(3'b000), .out(multiplexer_1_out), .sel(or_1_out));
  or or_1 (or_1_out, and_1_out, comparator_1_eq);
  Register #(.width(3)) Counter (.D(multiplexer_1_out), .en(1'b1), .clk(clk_out), .Q(Counter_q), .clr(reset_out));
  Adder #(.width(3)) adder_1 (.a(Counter_q), .b(3'b001), .out(adder_1_out));  // open: cin, cout
  Comparator #(.width(3)) comparator_1 (.a(adder_1_out), .b(3'b101), .eq(comparator_1_eq));  // open: gt, lt
  ConditionEncoding conditionencoding_1 (
    .Z(alu_1_zero), .N(alu_1_negative), .V(alu_1_overflow), .Condition(cpu_out[29:27]),
    .C(conditionencoding_1_c));
  Decoder #(.enable("false"), .select(3)) decoder_1 (
    .out0(decoder_1_out0), .out1(decoder_1_out1), .out2(decoder_1_out2), .out3(decoder_1_out3),
    .out4(decoder_1_out4), .sel(Counter_q));  // open: out5, out6, out7
  and and_1 (and_1_out, decoder_1_out2, conditionencoding_1_c, decoder_2_out1);
  Register #(.width(16)) PC (.D(adder_2_out), .en(or_2_out), .clk(clk_out), .Q(cpu_out[47:32]), .clr(reset_out));
  or or_2 (or_2_out, decoder_1_out0, and_1_out);
  or or_3 (or_3_out, decoder_2_out0, decoder_2_out2);
  Adder #(.width(16)) adder_2 (.a(cpu_out[47:32]), .b(multiplexer_2_out), .out(adder_2_out));  // open: cin, cout
  Multiplexer #(.width(16)) multiplexer_2 (
    .in0(16'h1), .in1(bit_extender_1_out), .out(multiplexer_2_out), .sel(and_1_out));
  and and_2 (and_2_out, or_3_out, decoder_1_out4);
  Multiplexer #(.width(3)) multiplexer_3 (
    .in0(cpu_out[18:16]), .in1(cpu_out[25:23]), .out(multiplexer_3_out), .sel(decoder_2_out3));
  ROM #(.addrWidth(16), .dataWidth(16)) InsMem (.addr(cpu_out[47:32]), .data(InsMem_data));
  assign bit_extender_1_out = {{13{cpu_out[25]}}, cpu_out[25:23]};  // Bit_Extender bit_extender_1
  RegisterFile registerfile_1 (
    .Addr_A(cpu_out[22:20]), .Addr_B(multiplexer_3_out), .Addr_C(cpu_out[25:23]), .we(and_2_out),
    .clk(clk_out), .reset(reset_out), .C(RW_q), .A(registerfile_1_a), .B(registerfile_1_b));
  Multiplexer #(.width(3)) multiplexer_4 (
    .in0(cpu_out[29:27]), .in1(3'b001), .out(multiplexer_4_out), .sel(decoder_2_out1));
  Register #(.width(16)) RA (.D(registerfile_1_a), .en(decoder_1_out1), .clk(clk_out), .Q(RA_q), .clr(reset_out));
  Register #(.width(16)) RB (.D(registerfile_1_b), .en(decoder_1_out1), .clk(clk_out), .Q(RB_q), .clr(reset_out));
  Multiplexer #(.width(16)) multiplexer_5 (
    .in0(RB_q), .in1(bit_extender_2_out), .out(multiplexer_5_out), .sel(cpu_out[26]));
  assign bit_extender_2_out = {{12{cpu_out[19]}}, cpu_out[19:16]};  // Bit_Extender bit_extender_2
  Register #(.width(16)) IR (.D(InsMem_data), .en(decoder_1_out0), .clk(clk_out), .Q(cpu_out[31:16]), .clr(reset_out));
  Register #(.width(16)) RZ (.D(alu_1_c), .en(decoder_1_out2), .clk(clk_out), .Q(cpu_out[15:0]), .clr(reset_out));
  ALU alu_1 (
    .A(RA_q), .B(multiplexer_5_out), .fun(multiplexer_4_out), .C(alu_1_c), .negative(alu_1_negative),
    .zero(alu_1_zero), .overflow(alu_1_overflow));  // open: carry
  Register #(.width(16)) RD (.D(RB_q), .en(decoder_1_out2), .clk(clk_out), .Q(RD_q), .clr(reset_out));
  Decoder #(.enable("false"), .select(2)) decoder_2 (
    .out0(decoder_2_out0), .out1(decoder_2_out1), .out2(decoder_2_out2), .out3(decoder_2_out3),
    .sel(cpu_out[31:30]));
  RAM #(.addrWidth(16), .dataWidth(16), .enables("line")) ram_1 (
    .addr(cpu_out[15:0]), .we(and_3_out), .clk(clk_out), .din(RD_q), .dout(ram_1_dout));
  and and_3 (and_3_out, decoder_1_out3, decoder_2_out3);
  Multiplexer #(.width(16)) multiplexer_6 (
    .in0(cpu_out[15:0]), .in1(ram_1_dout), .out(multiplexer_6_out), .sel(decoder_2_out2));
  Register #(.width(16)) RW (.D(multiplexer_6_out), .en(decoder_1_out3), .clk(clk_out), .Q(RW_q), .clr(reset_out));
  Comparator #(.width(16)) comparator_2 (.a(cpu_out[31:16]), .b(16'h4380), .eq(halt));  // open: gt, lt

  // Notes on the sheet:
  //   Your program will stop when the halt is 1
  //   The cpu_out is a debug signal to check whether your code works or not
endmodule

module ALU (
  input  [2:0] fun,
  input  [15:0] A,
  input  [15:0] B,
  output [15:0] C,
  output negative,
  output zero,
  output carry,
  output overflow
);

  wire add_sub_1_msb_eq, xor_1_out;
  wire [14:0] add_sub_1_sum;
  wire [15:0] and_sixteen_1_c, nor_sixteen_1_c, or_sixteen_1_c, shifter_1_out, shifter_2_out, shifter_3_out;
  wire [15:15] add_sub_1_sum_2;

  and and_1 (overflow, add_sub_1_msb_eq, xor_1_out);
  xor xor_1 (xor_1_out, A[15], add_sub_1_sum_2[15]);
  Shifter #(.width(16)) shifter_1 (.in(A), .\dist (B[3:0]), .out(shifter_1_out));
  Shifter #(.shift("lr"), .width(16)) shifter_2 (.in(A), .\dist (B[3:0]), .out(shifter_2_out));
  Shifter #(.shift("ar"), .width(16)) shifter_3 (.in(A), .\dist (B[3:0]), .out(shifter_3_out));
  ADD_SUB add_sub_1 (
    .A(A), .B(B), .Cin(fun[0]), .Sum({add_sub_1_sum_2[15], add_sub_1_sum}), .Cout(carry),
    .MSB_EQ(add_sub_1_msb_eq));
  AND_SIXTEEN and_sixteen_1 (.A(A), .B(B), .C(and_sixteen_1_c));
  OR_SIXTEEN or_sixteen_1 (.A(A), .B(B), .C(or_sixteen_1_c));
  NOR_SIXTEEN nor_sixteen_1 (.A(B), .B(A), .C(nor_sixteen_1_c));
  nor nor_1 (zero, C[15], C[14], C[13], C[12], C[11], C[10], C[9], C[8], C[7], C[6], C[5], C[4], C[3], C[2], C[1], C[0]);
  Multiplexer #(.select(3), .width(16)) multiplexer_1 (
    .in0({add_sub_1_sum_2[15], add_sub_1_sum}), .in1({add_sub_1_sum_2[15], add_sub_1_sum}),
    .in2(and_sixteen_1_c), .in3(or_sixteen_1_c), .in4(nor_sixteen_1_c), .in5(shifter_1_out),
    .in6(shifter_2_out), .in7(shifter_3_out), .out(C), .sel(fun));

  assign negative = C[15];
endmodule

module RegisterFile (
  input  [2:0] Addr_A,
  input  [2:0] Addr_B,
  input  [2:0] Addr_C,
  input  we,
  input  clk,
  input  reset,
  input  [15:0] C,
  output [15:0] A,
  output [15:0] B
);

  wire and_1_out, and_2_out, and_3_out, and_4_out, and_5_out, and_6_out, and_7_out, and_8_out,
       decoder_1_out0, decoder_1_out1, decoder_1_out2, decoder_1_out3, decoder_1_out4, decoder_1_out5,
       decoder_1_out6, decoder_1_out7;
  wire [15:0] R0_q, R1_q, R2_q, R3_q, R4_q, R5_q, R6_q, R7_q;

  Decoder #(.enable("false"), .select(3)) decoder_1 (
    .out0(decoder_1_out0), .out1(decoder_1_out1), .out2(decoder_1_out2), .out3(decoder_1_out3),
    .out4(decoder_1_out4), .out5(decoder_1_out5), .out6(decoder_1_out6), .out7(decoder_1_out7), .sel(Addr_C));
  and and_1 (and_1_out, we, decoder_1_out0);
  and and_2 (and_2_out, we, decoder_1_out1);
  and and_3 (and_3_out, we, decoder_1_out2);
  and and_4 (and_4_out, we, decoder_1_out3);
  and and_5 (and_5_out, we, decoder_1_out4);
  and and_6 (and_6_out, we, decoder_1_out5);
  and and_7 (and_7_out, we, decoder_1_out6);
  and and_8 (and_8_out, we, decoder_1_out7);
  Register #(.width(16)) R0 (.D(C), .en(and_1_out), .clk(clk), .Q(R0_q), .clr(reset));
  Register #(.width(16)) R1 (.D(C), .en(and_2_out), .clk(clk), .Q(R1_q), .clr(reset));
  Register #(.width(16)) R2 (.D(C), .en(and_3_out), .clk(clk), .Q(R2_q), .clr(reset));
  Register #(.width(16)) R3 (.D(C), .en(and_4_out), .clk(clk), .Q(R3_q), .clr(reset));
  Register #(.width(16)) R4 (.D(C), .en(and_5_out), .clk(clk), .Q(R4_q), .clr(reset));
  Register #(.width(16)) R5 (.D(C), .en(and_6_out), .clk(clk), .Q(R5_q), .clr(reset));
  Register #(.width(16)) R6 (.D(C), .en(and_7_out), .clk(clk), .Q(R6_q), .clr(reset));
  Register #(.width(16)) R7 (.D(C), .en(and_8_out), .clk(clk), .Q(R7_q), .clr(reset));
  Multiplexer #(.select(3), .width(16)) multiplexer_1 (
    .in0(R0_q), .in1(R1_q), .in2(R2_q), .in3(R3_q), .in4(R4_q), .in5(R5_q), .in6(R6_q), .in7(R7_q), .out(A),
    .sel(Addr_A));
  Multiplexer #(.select(3), .width(16)) multiplexer_2 (
    .in0(R0_q), .in1(R1_q), .in2(R2_q), .in3(R3_q), .in4(R4_q), .in5(R5_q), .in6(R6_q), .in7(R7_q), .out(B),
    .sel(Addr_B));

  // Notes on the sheet:
  //   Do not modify placement of these inputs and outputs
endmodule

module RegisterFileTester (
  output halt,
  output [15:0] A,
  output [15:0] B,
  output clk
);

  wire undriven;
  wire [2:0] Addr_A_data, Addr_B_data, Addr_C_data;
  wire [3:0] adder_1_out, addr_q;
  wire [15:0] C_data;

  Clock clock_1 (.out(clk));
  ROM #(.addrWidth(4), .dataWidth(3)) Addr_A (.addr(addr_q), .data(Addr_A_data));
  ROM #(.addrWidth(4), .dataWidth(3)) Addr_B (.addr(addr_q), .data(Addr_B_data));
  ROM #(.addrWidth(4), .dataWidth(3)) Addr_C (.addr(addr_q), .data(Addr_C_data));
  ROM #(.addrWidth(4), .dataWidth(1)) we (.addr(addr_q));  // open: data
  ROM #(.addrWidth(4), .dataWidth(16)) C (.addr(addr_q), .data(C_data));
  Adder #(.width(4)) adder_1 (.a(addr_q), .b(4'b0001), .out(adder_1_out), .cin(1'b0));  // open: cout
  Register #(.width(4)) addr (.D(adder_1_out), .en(1'b1), .clk(clk), .Q(addr_q), .clr(1'b0));
  Comparator #(.width(4)) comparator_1 (.a(addr_q), .b(4'b1111), .eq(halt));  // open: gt, lt
  RegisterFile registerfile_1 (
    .Addr_A(Addr_A_data), .Addr_B(Addr_B_data), .Addr_C(Addr_C_data), .we(undriven), .clk(clk), .reset(1'b0),
    .C(C_data), .A(A), .B(B));

  // Notes on the sheet:
  //   contents of Addr_A (hex, n*v repeats v):
  //   5 2 7 3 2 0 2 6 2 4 1 3 5 5 2 6
  //   contents of Addr_B (hex, n*v repeats v):
  //   4 4 6 0 2 3 5 5 5 0 0 4 5 3 7 5
  //   contents of Addr_C (hex, n*v repeats v):
  //   0 5 0 5 5 7 2 3 6 4 0 4 7 7 4 6
  //   contents of we (hex, n*v repeats v):
  //   0 0 0 1 0 0 1 0 0 0 1 1 0 0 1 1
  //   contents of C (hex, n*v repeats v):
  //   1 4 c f 0 5 9 7 c b 9 f b 9 1 e
endmodule

module AND_SIXTEEN (
  input  [15:0] A,
  input  [15:0] B,
  output [15:0] C
);

  and and_1 (C[0], A[0], B[0]);
  and and_2 (C[1], A[1], B[1]);
  and and_3 (C[2], A[2], B[2]);
  and and_4 (C[3], A[3], B[3]);
  and and_5 (C[4], A[4], B[4]);
  and and_6 (C[5], A[5], B[5]);
  and and_7 (C[6], A[6], B[6]);
  and and_8 (C[7], A[7], B[7]);
  and and_9 (C[8], A[8], B[8]);
  and and_10 (C[9], A[9], B[9]);
  and and_11 (C[10], A[10], B[10]);
  and and_12 (C[11], A[11], B[11]);
  and and_13 (C[12], A[12], B[12]);
  and and_14 (C[13], A[13], B[13]);
  and and_15 (C[14], A[14], B[14]);
  and and_16 (C[15], A[15], B[15]);
endmodule

module OR_SIXTEEN (
  input  [15:0] A,
  input  [15:0] B,
  output [15:0] C
);

  or or_1 (C[0], A[0], B[0]);
  or or_2 (C[1], A[1], B[1]);
  or or_3 (C[2], A[2], B[2]);
  or or_4 (C[3], A[3], B[3]);
  or or_5 (C[4], A[4], B[4]);
  or or_6 (C[5], A[5], B[5]);
  or or_7 (C[6], A[6], B[6]);
  or or_8 (C[7], A[7], B[7]);
  or or_9 (C[8], A[8], B[8]);
  or or_10 (C[9], A[9], B[9]);
  or or_11 (C[10], A[10], B[10]);
  or or_12 (C[11], A[11], B[11]);
  or or_13 (C[12], A[12], B[12]);
  or or_14 (C[13], A[13], B[13]);
  or or_15 (C[14], A[14], B[14]);
  or or_16 (C[15], A[15], B[15]);
endmodule

module NOR_SIXTEEN (
  input  [15:0] A,
  input  [15:0] B,
  output [15:0] C
);

  nor nor_1 (C[0], A[0], B[0]);
  nor nor_2 (C[1], A[1], B[1]);
  nor nor_3 (C[2], A[2], B[2]);
  nor nor_4 (C[3], A[3], B[3]);
  nor nor_5 (C[4], A[4], B[4]);
  nor nor_6 (C[5], A[5], B[5]);
  nor nor_7 (C[6], A[6], B[6]);
  nor nor_8 (C[7], A[7], B[7]);
  nor nor_9 (C[8], A[8], B[8]);
  nor nor_10 (C[9], A[9], B[9]);
  nor nor_11 (C[10], A[10], B[10]);
  nor nor_12 (C[11], A[11], B[11]);
  nor nor_13 (C[12], A[12], B[12]);
  nor nor_14 (C[13], A[13], B[13]);
  nor nor_15 (C[14], A[14], B[14]);
  nor nor_16 (C[15], A[15], B[15]);
endmodule

module ADD_SUB (
  input  [15:0] A,
  input  [15:0] B,
  input  Cin,
  output [15:0] Sum,
  output Cout,
  output MSB_EQ
);

  wire not_1_out, not_2_out, not_3_out, not_4_out, not_5_out, not_6_out, not_7_out, not_8_out, not_9_out,
       not_10_out, not_11_out, not_12_out, not_13_out, not_14_out, not_15_out, not_16_out;
  wire [15:0] multiplexer_1_out;

  not not_1 (not_1_out, B[0]);
  not not_2 (not_2_out, B[1]);
  not not_3 (not_3_out, B[2]);
  not not_4 (not_4_out, B[3]);
  not not_5 (not_5_out, B[4]);
  not not_6 (not_6_out, B[5]);
  not not_7 (not_7_out, B[6]);
  not not_8 (not_8_out, B[7]);
  not not_9 (not_9_out, B[8]);
  not not_10 (not_10_out, B[9]);
  not not_11 (not_11_out, B[10]);
  not not_12 (not_12_out, B[11]);
  not not_13 (not_13_out, B[12]);
  not not_14 (not_14_out, B[13]);
  not not_15 (not_15_out, B[14]);
  not not_16 (not_16_out, B[15]);
  Multiplexer multiplexer_1 (.in0(B[0]), .in1(not_1_out), .out(multiplexer_1_out[0]), .sel(Cin));
  Multiplexer multiplexer_2 (.in0(B[1]), .in1(not_2_out), .out(multiplexer_1_out[1]), .sel(Cin));
  Multiplexer multiplexer_3 (.in0(B[2]), .in1(not_3_out), .out(multiplexer_1_out[2]), .sel(Cin));
  Multiplexer multiplexer_4 (.in0(B[3]), .in1(not_4_out), .out(multiplexer_1_out[3]), .sel(Cin));
  Multiplexer multiplexer_5 (.in0(B[4]), .in1(not_5_out), .out(multiplexer_1_out[4]), .sel(Cin));
  Multiplexer multiplexer_6 (.in0(B[5]), .in1(not_6_out), .out(multiplexer_1_out[5]), .sel(Cin));
  Multiplexer multiplexer_7 (.in0(B[6]), .in1(not_7_out), .out(multiplexer_1_out[6]), .sel(Cin));
  Multiplexer multiplexer_8 (.in0(B[7]), .in1(not_8_out), .out(multiplexer_1_out[7]), .sel(Cin));
  Multiplexer multiplexer_9 (.in0(B[8]), .in1(not_9_out), .out(multiplexer_1_out[8]), .sel(Cin));
  Multiplexer multiplexer_10 (.in0(B[9]), .in1(not_10_out), .out(multiplexer_1_out[9]), .sel(Cin));
  Multiplexer multiplexer_11 (.in0(B[10]), .in1(not_11_out), .out(multiplexer_1_out[10]), .sel(Cin));
  Multiplexer multiplexer_12 (.in0(B[11]), .in1(not_12_out), .out(multiplexer_1_out[11]), .sel(Cin));
  Multiplexer multiplexer_13 (.in0(B[12]), .in1(not_13_out), .out(multiplexer_1_out[12]), .sel(Cin));
  Multiplexer multiplexer_14 (.in0(B[13]), .in1(not_14_out), .out(multiplexer_1_out[13]), .sel(Cin));
  Multiplexer multiplexer_15 (.in0(B[14]), .in1(not_15_out), .out(multiplexer_1_out[14]), .sel(Cin));
  Multiplexer multiplexer_16 (.in0(B[15]), .in1(not_16_out), .out(multiplexer_1_out[15]), .sel(Cin));
  Adder #(.width(16)) adder_1 (.a(A), .b(multiplexer_1_out), .out(Sum), .cin(Cin), .cout(Cout));
  xnor xnor_1 (MSB_EQ, A[15], multiplexer_1_out[15]);
endmodule

module ConditionEncoding (
  input  Z,
  input  N,
  input  V,
  input  [2:0] Condition,
  output C
);

  wire and_1_out, and_2_out, and_3_out, and_4_out, and_5_out, and_6_out, decoder_1_out0, decoder_1_out1,
       decoder_1_out2, decoder_1_out3, decoder_1_out4, decoder_1_out5, not_1_out, or_1_out, xnor_1_out,
       xor_1_out;

  Decoder #(.enable("false"), .select(3)) decoder_1 (
    .out0(decoder_1_out0), .out1(decoder_1_out1), .out2(decoder_1_out2), .out3(decoder_1_out3),
    .out4(decoder_1_out4), .out5(decoder_1_out5), .sel(Condition));  // open: out6, out7
  xor xor_1 (xor_1_out, N, V);
  xnor xnor_1 (xnor_1_out, N, V);
  and and_1 (and_1_out, Z, decoder_1_out0);
  not not_1 (not_1_out, Z);
  or or_1 (or_1_out, Z, xor_1_out);
  and and_2 (and_2_out, decoder_1_out1, not_1_out);
  and and_3 (and_3_out, decoder_1_out2, xor_1_out);
  and and_4 (and_4_out, or_1_out, decoder_1_out3);
  and and_5 (and_5_out, not_1_out, xnor_1_out, decoder_1_out4);
  and and_6 (and_6_out, xnor_1_out, decoder_1_out5);
  or or_2 (C, and_1_out, and_2_out, and_3_out, and_4_out, and_5_out, and_6_out);
endmodule
